# Fritzing sketch breadboard (saved by Fritzing 0.9.4)
breadboards: 1

parts:
  Part1 = Arduino Uno (Rev3)
  IC1 = L293D [package=THT]
  R1 = Resistor [tolerance=±5% resistance=10k package=THT]
  R2 = Resistor [tolerance=±5% resistance=10k package=THT]
  R3 = Resistor [tolerance=±5% resistance=10k package=THT]
  R4 = Resistor [tolerance=±5% resistance=10k package=THT]
  S1 = Pushbutton [package="[THT]"]
  S2 = Pushbutton [package="[THT]"]
  S3 = Pushbutton [package="[THT]"]
  S4 = Pushbutton [package="[THT]"]
  M1 = DC Motor
  Part2 = Thumb Joystick
  M2 = DC Motor
  HLK-PM1 = HLK-PM12 [part_number=HLK-PM12]

nets:
  N1: Part1.A0, Part2.HORZ
  N2: Part1.A1, Part2.VERT
  N3: Part1.A2, Part2.SEL
  N4: Part1.D8, IC1.In_2
  N5: Part1.D9_PWM, IC1.In_4
  N6: Part1.D10_PWM/SS, IC1.Enable_1
  N7: Part1.D11_PWM/MOSI, IC1.Enable_2
  N8: Part1.D12/MISO, IC1.In_3
  N9: Part1.D2, R1.Pin_0, S1.Pin_3, S1.Pin_4
  N10: Part1.D3_PWM, R4.Pin_0, S4.Pin_3, S4.Pin_4
  N11: Part1.D4, R3.Pin_0, S2.Pin_3, S2.Pin_4
  N12: Part1.D5_PWM, R2.Pin_0, S3.Pin_3, S3.Pin_4
  N13: Part1.D6_PWM, IC1.In_1
  5V: Part1.5V, IC1.+V, R1.Pin_1, R2.Pin_1, R3.Pin_1, R4.Pin_1, Part2.VCC
  GND: Part1.GND, IC1.0V, S1.Pin_1, S1.Pin_2, S2.Pin_1, S2.Pin_2, S3.Pin_1, S3.Pin_2, S4.Pin_1, S4.Pin_2, Part2.GND, HLK-PM1.-Vo
  N14: IC1.Out_1_(_Controlled_by_Enable_1_), M2.pin_2
  N15: IC1.Out_2_(_Controlled_by_Enable_1_), M2.pin_1
  N16: IC1.+Vmotor, HLK-PM1.+Vo
  N17: IC1.Out_3_(_Controlled_by_Enable_2_), M1.pin_1
  N18: IC1.Out_4_(_Controlled_by_Enable_2_), M1.pin_2
